// Logisim project project.circ as structural Verilog
module main (
  input  click,
  input  [5:0] bus_0
);

  wire _1, _2, _3, _4, _5, _6, _7, _8, _9, _10, _11, _12, _13, _14, _15, _16, _17, _18, _19, _20, _21, _22,
       _23, _24, _25, _26, _27, _28, _29, _30, _31, _32, _33, _34, _35, _36, _37, _38, _39, _40, _41, _42,
       _43, _44, _45, _46, _47, _48, _49, _50, _51, _52, _53, _54, _55, _56, _57, _58, _59, _60, _61, _62,
       _63, _64, clk;
  wire [3:0] matrix_1_current_column, matrix_2_current_column, matrix_3_current_column,
       matrix_4_current_column, matrix_5_current_column, matrix_6_current_column, matrix_7_current_column,
       matrix_8_current_column, matrix_9_current_column, matrix_10_current_column, matrix_11_current_column,
       matrix_12_current_column, matrix_13_current_column, matrix_14_current_column,
       matrix_15_current_column, matrix_16_current_column, matrix_17_current_column,
       matrix_18_current_column, matrix_19_current_column, matrix_20_current_column,
       matrix_21_current_column, matrix_22_current_column, matrix_23_current_column,
       matrix_24_current_column, matrix_25_current_column, matrix_26_current_column,
       matrix_27_current_column, matrix_28_current_column, matrix_29_current_column,
       matrix_30_current_column, matrix_31_current_column, matrix_32_current_column,
       matrix_33_current_column, matrix_34_current_column, matrix_35_current_column,
       matrix_36_current_column, matrix_37_current_column, matrix_38_current_column,
       matrix_39_current_column, matrix_40_current_column, matrix_41_current_column,
       matrix_42_current_column, matrix_43_current_column, matrix_44_current_column,
       matrix_45_current_column, matrix_46_current_column, matrix_47_current_column,
       matrix_48_current_column, matrix_49_current_column, matrix_50_current_column,
       matrix_51_current_column, matrix_52_current_column, matrix_53_current_column,
       matrix_54_current_column, matrix_55_current_column, matrix_56_current_column,
       matrix_57_current_column, matrix_58_current_column, matrix_59_current_column,
       matrix_60_current_column, matrix_61_current_column, matrix_62_current_column,
       matrix_63_current_column, matrix_64_current_column;
  wire [15:0] _1a1, _1a2, _1a3, _1a4, _1a5, _1a6, _1a7, _1a8, _1a9, _1a10, _1a11, _1a12, _1a13, _1a14, _1a15,
       _1a16, _1b1, _1b2, _1b3, _1b4, _1b5, _1b6, _1b7, _1b8, _1b9, _1b10, _1b11, _1b12, _1b13, _1b14, _1b15,
       _1b16, _1c1, _1c2, _1c3, _1c4, _1c5, _1c6, _1c7, _1c8, _1c9, _1c10, _1c11, _1c12, _1c13, _1c14, _1c15,
       _1c16, _1d1, _1d2, _1d3, _1d4, _1d5, _1d6, _1d7, _1d8, _1d9, _1d10, _1d11, _1d12, _1d13, _1d14, _1d15,
       _1d16, _1e1, _1e2, _1e3, _1e4, _1e5, _1e6, _1e7, _1e8, _1e9, _1e10, _1e11, _1e12, _1e13, _1e14, _1e15,
       _1e16, _1f1, _1f2, _1f3, _1f4, _1f5, _1f6, _1f7, _1f8, _1f9, _1f10, _1f11, _1f12, _1f13, _1f14, _1f15,
       _1f16, _1g1, _1g2, _1g3, _1g4, _1g5, _1g6, _1g7, _1g8, _1g9, _1g10, _1g11, _1g12, _1g13, _1g14, _1g15,
       _1g16, _1h1, _1h2, _1h3, _1h4, _1h5, _1h6, _1h7, _1h8, _1h9, _1h10, _1h11, _1h12, _1h13, _1h14, _1h15,
       _1h16, _2a1, _2a2, _2a3, _2a4, _2a5, _2a6, _2a7, _2a8, _2a9, _2a10, _2a11, _2a12, _2a13, _2a14, _2a15,
       _2a16, _2b1, _2b2, _2b3, _2b4, _2b5, _2b6, _2b7, _2b8, _2b9, _2b10, _2b11, _2b12, _2b13, _2b14, _2b15,
       _2b16, _2c1, _2c2, _2c3, _2c4, _2c5, _2c6, _2c7, _2c8, _2c9, _2c10, _2c11, _2c12, _2c13, _2c14, _2c15,
       _2c16, _2d1, _2d2, _2d3, _2d4, _2d5, _2d6, _2d7, _2d8, _2d9, _2d10, _2d11, _2d12, _2d13, _2d14, _2d15,
       _2d16, _2e1, _2e2, _2e3, _2e4, _2e5, _2e6, _2e7, _2e8, _2e9, _2e10, _2e11, _2e12, _2e13, _2e14, _2e15,
       _2e16, _2f1, _2f2, _2f3, _2f4, _2f5, _2f6, _2f7, _2f8, _2f9, _2f10, _2f11, _2f12, _2f13, _2f14, _2f15,
       _2f16, _2g1, _2g2, _2g3, _2g4, _2g5, _2g6, _2g7, _2g8, _2g9, _2g10, _2g11, _2g12, _2g13, _2g14, _2g15,
       _2g16, _2h1, _2h2, _2h3, _2h4, _2h5, _2h6, _2h7, _2h8, _2h9, _2h10, _2h11, _2h12, _2h13, _2h14, _2h15,
       _2h16, _3a1, _3a2, _3a3, _3a4, _3a5, _3a6, _3a7, _3a8, _3a9, _3a10, _3a11, _3a12, _3a13, _3a14, _3a15,
       _3a16, _3b1, _3b2, _3b3, _3b4, _3b5, _3b6, _3b7, _3b8, _3b9, _3b10, _3b11, _3b12, _3b13, _3b14, _3b15,
       _3b16, _3c1, _3c2, _3c3, _3c4, _3c5, _3c6, _3c7, _3c8, _3c9, _3c10, _3c11, _3c12, _3c13, _3c14, _3c15,
       _3c16, _3d1, _3d2, _3d3, _3d4, _3d5, _3d6, _3d7, _3d8, _3d9, _3d10, _3d11, _3d12, _3d13, _3d14, _3d15,
       _3d16, _3e1, _3e2, _3e3, _3e4, _3e5, _3e6, _3e7, _3e8, _3e9, _3e10, _3e11, _3e12, _3e13, _3e14, _3e15,
       _3e16, _3f1, _3f2, _3f3, _3f4, _3f5, _3f6, _3f7, _3f8, _3f9, _3f10, _3f11, _3f12, _3f13, _3f14, _3f15,
       _3f16, _3g1, _3g2, _3g3, _3g4, _3g5, _3g6, _3g7, _3g8, _3g9, _3g10, _3g11, _3g12, _3g13, _3g14, _3g15,
       _3g16, _3h1, _3h2, _3h3, _3h4, _3h5, _3h6, _3h7, _3h8, _3h9, _3h10, _3h11, _3h12, _3h13, _3h14, _3h15,
       _3h16, _4a1, _4a2, _4a3, _4a4, _4a5, _4a6, _4a7, _4a8, _4a9, _4a10, _4a11, _4a12, _4a13, _4a14, _4a15,
       _4a16, _4b1, _4b2, _4b3, _4b4, _4b5, _4b6, _4b7, _4b8, _4b9, _4b10, _4b11, _4b12, _4b13, _4b14, _4b15,
       _4b16, _4c1, _4c2, _4c3, _4c4, _4c5, _4c6, _4c7, _4c8, _4c9, _4c10, _4c11, _4c12, _4c13, _4c14, _4c15,
       _4c16, _4d1, _4d2, _4d3, _4d4, _4d5, _4d6, _4d7, _4d8, _4d9, _4d10, _4d11, _4d12, _4d13, _4d14, _4d15,
       _4d16, _4e1, _4e2, _4e3, _4e4, _4e5, _4e6, _4e7, _4e8, _4e9, _4e10, _4e11, _4e12, _4e13, _4e14, _4e15,
       _4e16, _4f1, _4f2, _4f3, _4f4, _4f5, _4f6, _4f7, _4f8, _4f9, _4f10, _4f11, _4f12, _4f13, _4f14, _4f15,
       _4f16, _4g1, _4g2, _4g3, _4g4, _4g5, _4g6, _4g7, _4g8, _4g9, _4g10, _4g11, _4g12, _4g13, _4g14, _4g15,
       _4g16, _4h1, _4h2, _4h3, _4h4, _4h5, _4h6, _4h7, _4h8, _4h9, _4h10, _4h11, _4h12, _4h13, _4h14, _4h15,
       _4h16, _5a1, _5a2, _5a3, _5a4, _5a5, _5a6, _5a7, _5a8, _5a9, _5a10, _5a11, _5a12, _5a13, _5a14, _5a15,
       _5a16, _5b1, _5b2, _5b3, _5b4, _5b5, _5b6, _5b7, _5b8, _5b9, _5b10, _5b11, _5b12, _5b13, _5b14, _5b15,
       _5b16, _5c1, _5c2, _5c3, _5c4, _5c5, _5c6, _5c7, _5c8, _5c9, _5c10, _5c11, _5c12, _5c13, _5c14, _5c15,
       _5c16, _5d1, _5d2, _5d3, _5d4, _5d5, _5d6, _5d7, _5d8, _5d9, _5d10, _5d11, _5d12, _5d13, _5d14, _5d15,
       _5d16, _5e1, _5e2, _5e3, _5e4, _5e5, _5e6, _5e7, _5e8, _5e9, _5e10, _5e11, _5e12, _5e13, _5e14, _5e15,
       _5e16, _5f1, _5f2, _5f3, _5f4, _5f5, _5f6, _5f7, _5f8, _5f9, _5f10, _5f11, _5f12, _5f13, _5f14, _5f15,
       _5f16, _5g1, _5g2, _5g3, _5g4, _5g5, _5g6, _5g7, _5g8, _5g9, _5g10, _5g11, _5g12, _5g13, _5g14, _5g15,
       _5g16, _5h1, _5h2, _5h3, _5h4, _5h5, _5h6, _5h7, _5h8, _5h9, _5h10, _5h11, _5h12, _5h13, _5h14, _5h15,
       _5h16, _6a1, _6a2, _6a3, _6a4, _6a5, _6a6, _6a7, _6a8, _6a9, _6a10, _6a11, _6a12, _6a13, _6a14, _6a15,
       _6a16, _6b1, _6b2, _6b3, _6b4, _6b5, _6b6, _6b7, _6b8, _6b9, _6b10, _6b11, _6b12, _6b13, _6b14, _6b15,
       _6b16, _6c1, _6c2, _6c3, _6c4, _6c5, _6c6, _6c7, _6c8, _6c9, _6c10, _6c11, _6c12, _6c13, _6c14, _6c15,
       _6c16, _6d1, _6d2, _6d3, _6d4, _6d5, _6d6, _6d7, _6d8, _6d9, _6d10, _6d11, _6d12, _6d13, _6d14, _6d15,
       _6d16, _6e1, _6e2, _6e3, _6e4, _6e5, _6e6, _6e7, _6e8, _6e9, _6e10, _6e11, _6e12, _6e13, _6e14, _6e15,
       _6e16, _6f1, _6f2, _6f3, _6f4, _6f5, _6f6, _6f7, _6f8, _6f9, _6f10, _6f11, _6f12, _6f13, _6f14, _6f15,
       _6f16, _6g1, _6g2, _6g3, _6g4, _6g5, _6g6, _6g7, _6g8, _6g9, _6g10, _6g11, _6g12, _6g13, _6g14, _6g15,
       _6g16, _6h1, _6h2, _6h3, _6h4, _6h5, _6h6, _6h7, _6h8, _6h9, _6h10, _6h11, _6h12, _6h13, _6h14, _6h15,
       _6h16, _7a1, _7a2, _7a3, _7a4, _7a5, _7a6, _7a7, _7a8, _7a9, _7a10, _7a11, _7a12, _7a13, _7a14, _7a15,
       _7a16, _7b1, _7b2, _7b3, _7b4, _7b5, _7b6, _7b7, _7b8, _7b9, _7b10, _7b11, _7b12, _7b13, _7b14, _7b15,
       _7b16, _7c1, _7c2, _7c3, _7c4, _7c5, _7c6, _7c7, _7c8, _7c9, _7c10, _7c11, _7c12, _7c13, _7c14, _7c15,
       _7c16, _7d1, _7d2, _7d3, _7d4, _7d5, _7d6, _7d7, _7d8, _7d9, _7d10, _7d11, _7d12, _7d13, _7d14, _7d15,
       _7d16, _7e1, _7e2, _7e3, _7e4, _7e5, _7e6, _7e7, _7e8, _7e9, _7e10, _7e11, _7e12, _7e13, _7e14, _7e15,
       _7e16, _7f1, _7f2, _7f3, _7f4, _7f5, _7f6, _7f7, _7f8, _7f9, _7f10, _7f11, _7f12, _7f13, _7f14, _7f15,
       _7f16, _7g1, _7g2, _7g3, _7g4, _7g5, _7g6, _7g7, _7g8, _7g9, _7g10, _7g11, _7g12, _7g13, _7g14, _7g15,
       _7g16, _7h1, _7h2, _7h3, _7h4, _7h5, _7h6, _7h7, _7h8, _7h9, _7h10, _7h11, _7h12, _7h13, _7h14, _7h15,
       _7h16, _8a1, _8a2, _8a3, _8a4, _8a5, _8a6, _8a7, _8a8, _8a9, _8a10, _8a11, _8a12, _8a13, _8a14, _8a15,
       _8a16, _8b1, _8b2, _8b3, _8b4, _8b5, _8b6, _8b7, _8b8, _8b9, _8b10, _8b11, _8b12, _8b13, _8b14, _8b15,
       _8b16, _8c1, _8c2, _8c3, _8c4, _8c5, _8c6, _8c7, _8c8, _8c9, _8c10, _8c11, _8c12, _8c13, _8c14, _8c15,
       _8c16, _8d1, _8d2, _8d3, _8d4, _8d5, _8d6, _8d7, _8d8, _8d9, _8d10, _8d11, _8d12, _8d13, _8d14, _8d15,
       _8d16, _8e1, _8e2, _8e3, _8e4, _8e5, _8e6, _8e7, _8e8, _8e9, _8e10, _8e11, _8e12, _8e13, _8e14, _8e15,
       _8e16, _8f1, _8f2, _8f3, _8f4, _8f5, _8f6, _8f7, _8f8, _8f9, _8f10, _8f11, _8f12, _8f13, _8f14, _8f15,
       _8f16, _8g1, _8g2, _8g3, _8g4, _8g5, _8g6, _8g7, _8g8, _8g9, _8g10, _8g11, _8g12, _8g13, _8g14, _8g15,
       _8g16, _8h1, _8h2, _8h3, _8h4, _8h5, _8h6, _8h7, _8h8, _8h9, _8h10, _8h11, _8h12, _8h13, _8h14, _8h15,
       _8h16;

  Clock clock_1 (.out(clk));
  frame frame_1 ();
  DotMatrix #(.matrixcols(16), .matrixrows(16)) dotmatrix_1 (
    .col0(_8a1), .col1(_8a2), .col2(_8a3), .col3(_8a4), .col4(_8a5), .col5(_8a6), .col6(_8a7), .col7(_8a8),
    .col8(_8a9), .col9(_8a10), .col10(_8a11), .col11(_8a12), .col12(_8a13), .col13(_8a14), .col14(_8a15),
    .col15(_8a16));
  DotMatrix #(.matrixcols(16), .matrixrows(16)) dotmatrix_2 (
    .col0(_7a1), .col1(_7a2), .col2(_7a3), .col3(_7a4), .col4(_7a5), .col5(_7a6), .col6(_7a7), .col7(_7a8),
    .col8(_7a9), .col9(_7a10), .col10(_7a11), .col11(_7a12), .col12(_7a13), .col13(_7a14), .col14(_7a15),
    .col15(_7a16));
  DotMatrix #(.matrixcols(16), .matrixrows(16)) dotmatrix_3 (
    .col0(_6a1), .col1(_6a2), .col2(_6a3), .col3(_6a4), .col4(_6a5), .col5(_6a6), .col6(_6a7), .col7(_6a8),
    .col8(_6a9), .col9(_6a10), .col10(_6a11), .col11(_6a12), .col12(_6a13), .col13(_6a14), .col14(_6a15),
    .col15(_6a16));
  DotMatrix #(.matrixcols(16), .matrixrows(16)) dotmatrix_4 (
    .col0(_5a1), .col1(_5a2), .col2(_5a3), .col3(_5a4), .col4(_5a5), .col5(_5a6), .col6(_5a7), .col7(_5a8),
    .col8(_5a9), .col9(_5a10), .col10(_5a11), .col11(_5a12), .col12(_5a13), .col13(_5a14), .col14(_5a15),
    .col15(_5a16));
  DotMatrix #(.matrixcols(16), .matrixrows(16)) dotmatrix_5 (
    .col0(_4a1), .col1(_4a2), .col2(_4a3), .col3(_4a4), .col4(_4a5), .col5(_4a6), .col6(_4a7), .col7(_4a8),
    .col8(_4a9), .col9(_4a10), .col10(_4a11), .col11(_4a12), .col12(_4a13), .col13(_4a14), .col14(_4a15),
    .col15(_4a16));
  DotMatrix #(.matrixcols(16), .matrixrows(16)) dotmatrix_6 (
    .col0(_3a1), .col1(_3a2), .col2(_3a3), .col3(_3a4), .col4(_3a5), .col5(_3a6), .col6(_3a7), .col7(_3a8),
    .col8(_3a9), .col9(_3a10), .col10(_3a11), .col11(_3a12), .col12(_3a13), .col13(_3a14), .col14(_3a15),
    .col15(_3a16));
  DotMatrix #(.matrixcols(16), .matrixrows(16)) dotmatrix_7 (
    .col0(_2a1), .col1(_2a2), .col2(_2a3), .col3(_2a4), .col4(_2a5), .col5(_2a6), .col6(_2a7), .col7(_2a8),
    .col8(_2a9), .col9(_2a10), .col10(_2a11), .col11(_2a12), .col12(_2a13), .col13(_2a14), .col14(_2a15),
    .col15(_2a16));
  DotMatrix #(.matrixcols(16), .matrixrows(16)) dotmatrix_8 (
    .col0(_1a1), .col1(_1a2), .col2(_1a3), .col3(_1a4), .col4(_1a5), .col5(_1a6), .col6(_1a7), .col7(_1a8),
    .col8(_1a9), .col9(_1a10), .col10(_1a11), .col11(_1a12), .col12(_1a13), .col13(_1a14), .col14(_1a15),
    .col15(_1a16));
  DotMatrix #(.matrixcols(16), .matrixrows(16)) dotmatrix_9 (
    .col0(_8b1), .col1(_8b2), .col2(_8b3), .col3(_8b4), .col4(_8b5), .col5(_8b6), .col6(_8b7), .col7(_8b8),
    .col8(_8b9), .col9(_8b10), .col10(_8b11), .col11(_8b12), .col12(_8b13), .col13(_8b14), .col14(_8b15),
    .col15(_8b16));
  DotMatrix #(.matrixcols(16), .matrixrows(16)) dotmatrix_10 (
    .col0(_7b1), .col1(_7b2), .col2(_7b3), .col3(_7b4), .col4(_7b5), .col5(_7b6), .col6(_7b7), .col7(_7b8),
    .col8(_7b9), .col9(_7b10), .col10(_7b11), .col11(_7b12), .col12(_7b13), .col13(_7b14), .col14(_7b15),
    .col15(_7b16));
  DotMatrix #(.matrixcols(16), .matrixrows(16)) dotmatrix_11 (
    .col0(_6b1), .col1(_6b2), .col2(_6b3), .col3(_6b4), .col4(_6b5), .col5(_6b6), .col6(_6b7), .col7(_6b8),
    .col8(_6b9), .col9(_6b10), .col10(_6b11), .col11(_6b12), .col12(_6b13), .col13(_6b14), .col14(_6b15),
    .col15(_6b16));
  DotMatrix #(.matrixcols(16), .matrixrows(16)) dotmatrix_12 (
    .col0(_5b1), .col1(_5b2), .col2(_5b3), .col3(_5b4), .col4(_5b5), .col5(_5b6), .col6(_5b7), .col7(_5b8),
    .col8(_5b9), .col9(_5b10), .col10(_5b11), .col11(_5b12), .col12(_5b13), .col13(_5b14), .col14(_5b15),
    .col15(_5b16));
  DotMatrix #(.matrixcols(16), .matrixrows(16)) dotmatrix_13 (
    .col0(_4b1), .col1(_4b2), .col2(_4b3), .col3(_4b4), .col4(_4b5), .col5(_4b6), .col6(_4b7), .col7(_4b8),
    .col8(_4b9), .col9(_4b10), .col10(_4b11), .col11(_4b12), .col12(_4b13), .col13(_4b14), .col14(_4b15),
    .col15(_4b16));
  DotMatrix #(.matrixcols(16), .matrixrows(16)) dotmatrix_14 (
    .col0(_3b1), .col1(_3b2), .col2(_3b3), .col3(_3b4), .col4(_3b5), .col5(_3b6), .col6(_3b7), .col7(_3b8),
    .col8(_3b9), .col9(_3b10), .col10(_3b11), .col11(_3b12), .col12(_3b13), .col13(_3b14), .col14(_3b15),
    .col15(_3b16));
  DotMatrix #(.matrixcols(16), .matrixrows(16)) dotmatrix_15 (
    .col0(_2b1), .col1(_2b2), .col2(_2b3), .col3(_2b4), .col4(_2b5), .col5(_2b6), .col6(_2b7), .col7(_2b8),
    .col8(_2b9), .col9(_2b10), .col10(_2b11), .col11(_2b12), .col12(_2b13), .col13(_2b14), .col14(_2b15),
    .col15(_2b16));
  DotMatrix #(.matrixcols(16), .matrixrows(16)) dotmatrix_16 (
    .col0(_1b1), .col1(_1b2), .col2(_1b3), .col3(_1b4), .col4(_1b5), .col5(_1b6), .col6(_1b7), .col7(_1b8),
    .col8(_1b9), .col9(_1b10), .col10(_1b11), .col11(_1b12), .col12(_1b13), .col13(_1b14), .col14(_1b15),
    .col15(_1b16));
  DotMatrix #(.matrixcols(16), .matrixrows(16)) dotmatrix_17 (
    .col0(_8c1), .col1(_8c2), .col2(_8c3), .col3(_8c4), .col4(_8c5), .col5(_8c6), .col6(_8c7), .col7(_8c8),
    .col8(_8c9), .col9(_8c10), .col10(_8c11), .col11(_8c12), .col12(_8c13), .col13(_8c14), .col14(_8c15),
    .col15(_8c16));
  DotMatrix #(.matrixcols(16), .matrixrows(16)) dotmatrix_18 (
    .col0(_7c1), .col1(_7c2), .col2(_7c3), .col3(_7c4), .col4(_7c5), .col5(_7c6), .col6(_7c7), .col7(_7c8),
    .col8(_7c9), .col9(_7c10), .col10(_7c11), .col11(_7c12), .col12(_7c13), .col13(_7c14), .col14(_7c15),
    .col15(_7c16));
  DotMatrix #(.matrixcols(16), .matrixrows(16)) dotmatrix_19 (
    .col0(_6c1), .col1(_6c2), .col2(_6c3), .col3(_6c4), .col4(_6c5), .col5(_6c6), .col6(_6c7), .col7(_6c8),
    .col8(_6c9), .col9(_6c10), .col10(_6c11), .col11(_6c12), .col12(_6c13), .col13(_6c14), .col14(_6c15),
    .col15(_6c16));
  DotMatrix #(.matrixcols(16), .matrixrows(16)) dotmatrix_20 (
    .col0(_5c1), .col1(_5c2), .col2(_5c3), .col3(_5c4), .col4(_5c5), .col5(_5c6), .col6(_5c7), .col7(_5c8),
    .col8(_5c9), .col9(_5c10), .col10(_5c11), .col11(_5c12), .col12(_5c13), .col13(_5c14), .col14(_5c15),
    .col15(_5c16));
  DotMatrix #(.matrixcols(16), .matrixrows(16)) dotmatrix_21 (
    .col0(_4c1), .col1(_4c2), .col2(_4c3), .col3(_4c4), .col4(_4c5), .col5(_4c6), .col6(_4c7), .col7(_4c8),
    .col8(_4c9), .col9(_4c10), .col10(_4c11), .col11(_4c12), .col12(_4c13), .col13(_4c14), .col14(_4c15),
    .col15(_4c16));
  DotMatrix #(.matrixcols(16), .matrixrows(16)) dotmatrix_22 (
    .col0(_3c1), .col1(_3c2), .col2(_3c3), .col3(_3c4), .col4(_3c5), .col5(_3c6), .col6(_3c7), .col7(_3c8),
    .col8(_3c9), .col9(_3c10), .col10(_3c11), .col11(_3c12), .col12(_3c13), .col13(_3c14), .col14(_3c15),
    .col15(_3c16));
  DotMatrix #(.matrixcols(16), .matrixrows(16)) dotmatrix_23 (
    .col0(_2c1), .col1(_2c2), .col2(_2c3), .col3(_2c4), .col4(_2c5), .col5(_2c6), .col6(_2c7), .col7(_2c8),
    .col8(_2c9), .col9(_2c10), .col10(_2c11), .col11(_2c12), .col12(_2c13), .col13(_2c14), .col14(_2c15),
    .col15(_2c16));
  DotMatrix #(.matrixcols(16), .matrixrows(16)) dotmatrix_24 (
    .col0(_1c1), .col1(_1c2), .col2(_1c3), .col3(_1c4), .col4(_1c5), .col5(_1c6), .col6(_1c7), .col7(_1c8),
    .col8(_1c9), .col9(_1c10), .col10(_1c11), .col11(_1c12), .col12(_1c13), .col13(_1c14), .col14(_1c15),
    .col15(_1c16));
  DotMatrix #(.matrixcols(16), .matrixrows(16)) dotmatrix_25 (
    .col0(_8d1), .col1(_8d2), .col2(_8d3), .col3(_8d4), .col4(_8d5), .col5(_8d6), .col6(_8d7), .col7(_8d8),
    .col8(_8d9), .col9(_8d10), .col10(_8d11), .col11(_8d12), .col12(_8d13), .col13(_8d14), .col14(_8d15),
    .col15(_8d16));
  DotMatrix #(.matrixcols(16), .matrixrows(16)) dotmatrix_26 (
    .col0(_7d1), .col1(_7d2), .col2(_7d3), .col3(_7d4), .col4(_7d5), .col5(_7d6), .col6(_7d7), .col7(_7d8),
    .col8(_7d9), .col9(_7d10), .col10(_7d11), .col11(_7d12), .col12(_7d13), .col13(_7d14), .col14(_7d15),
    .col15(_7d16));
  DotMatrix #(.matrixcols(16), .matrixrows(16)) dotmatrix_27 (
    .col0(_6d1), .col1(_6d2), .col2(_6d3), .col3(_6d4), .col4(_6d5), .col5(_6d6), .col6(_6d7), .col7(_6d8),
    .col8(_6d9), .col9(_6d10), .col10(_6d11), .col11(_6d12), .col12(_6d13), .col13(_6d14), .col14(_6d15),
    .col15(_6d16));
  DotMatrix #(.matrixcols(16), .matrixrows(16)) dotmatrix_28 (
    .col0(_5d1), .col1(_5d2), .col2(_5d3), .col3(_5d4), .col4(_5d5), .col5(_5d6), .col6(_5d7), .col7(_5d8),
    .col8(_5d9), .col9(_5d10), .col10(_5d11), .col11(_5d12), .col12(_5d13), .col13(_5d14), .col14(_5d15),
    .col15(_5d16));
  DotMatrix #(.matrixcols(16), .matrixrows(16)) dotmatrix_29 (
    .col0(_4d1), .col1(_4d2), .col2(_4d3), .col3(_4d4), .col4(_4d5), .col5(_4d6), .col6(_4d7), .col7(_4d8),
    .col8(_4d9), .col9(_4d10), .col10(_4d11), .col11(_4d12), .col12(_4d13), .col13(_4d14), .col14(_4d15),
    .col15(_4d16));
  DotMatrix #(.matrixcols(16), .matrixrows(16)) dotmatrix_30 (
    .col0(_3d1), .col1(_3d2), .col2(_3d3), .col3(_3d4), .col4(_3d5), .col5(_3d6), .col6(_3d7), .col7(_3d8),
    .col8(_3d9), .col9(_3d10), .col10(_3d11), .col11(_3d12), .col12(_3d13), .col13(_3d14), .col14(_3d15),
    .col15(_3d16));
  DotMatrix #(.matrixcols(16), .matrixrows(16)) dotmatrix_31 (
    .col0(_2d1), .col1(_2d2), .col2(_2d3), .col3(_2d4), .col4(_2d5), .col5(_2d6), .col6(_2d7), .col7(_2d8),
    .col8(_2d9), .col9(_2d10), .col10(_2d11), .col11(_2d12), .col12(_2d13), .col13(_2d14), .col14(_2d15),
    .col15(_2d16));
  DotMatrix #(.matrixcols(16), .matrixrows(16)) dotmatrix_32 (
    .col0(_1d1), .col1(_1d2), .col2(_1d3), .col3(_1d4), .col4(_1d5), .col5(_1d6), .col6(_1d7), .col7(_1d8),
    .col8(_1d9), .col9(_1d10), .col10(_1d11), .col11(_1d12), .col12(_1d13), .col13(_1d14), .col14(_1d15),
    .col15(_1d16));
  DotMatrix #(.matrixcols(16), .matrixrows(16)) dotmatrix_33 (
    .col0(_8e1), .col1(_8e2), .col2(_8e3), .col3(_8e4), .col4(_8e5), .col5(_8e6), .col6(_8e7), .col7(_8e8),
    .col8(_8e9), .col9(_8e10), .col10(_8e11), .col11(_8e12), .col12(_8e13), .col13(_8e14), .col14(_8e15),
    .col15(_8e16));
  DotMatrix #(.matrixcols(16), .matrixrows(16)) dotmatrix_34 (
    .col0(_7e1), .col1(_7e2), .col2(_7e3), .col3(_7e4), .col4(_7e5), .col5(_7e6), .col6(_7e7), .col7(_7e8),
    .col8(_7e9), .col9(_7e10), .col10(_7e11), .col11(_7e12), .col12(_7e13), .col13(_7e14), .col14(_7e15),
    .col15(_7e16));
  DotMatrix #(.matrixcols(16), .matrixrows(16)) dotmatrix_35 (
    .col0(_6e1), .col1(_6e2), .col2(_6e3), .col3(_6e4), .col4(_6e5), .col5(_6e6), .col6(_6e7), .col7(_6e8),
    .col8(_6e9), .col9(_6e10), .col10(_6e11), .col11(_6e12), .col12(_6e13), .col13(_6e14), .col14(_6e15),
    .col15(_6e16));
  DotMatrix #(.matrixcols(16), .matrixrows(16)) dotmatrix_36 (
    .col0(_5e1), .col1(_5e2), .col2(_5e3), .col3(_5e4), .col4(_5e5), .col5(_5e6), .col6(_5e7), .col7(_5e8),
    .col8(_5e9), .col9(_5e10), .col10(_5e11), .col11(_5e12), .col12(_5e13), .col13(_5e14), .col14(_5e15),
    .col15(_5e16));
  DotMatrix #(.matrixcols(16), .matrixrows(16)) dotmatrix_37 (
    .col0(_4e1), .col1(_4e2), .col2(_4e3), .col3(_4e4), .col4(_4e5), .col5(_4e6), .col6(_4e7), .col7(_4e8),
    .col8(_4e9), .col9(_4e10), .col10(_4e11), .col11(_4e12), .col12(_4e13), .col13(_4e14), .col14(_4e15),
    .col15(_4e16));
  DotMatrix #(.matrixcols(16), .matrixrows(16)) dotmatrix_38 (
    .col0(_3e1), .col1(_3e2), .col2(_3e3), .col3(_3e4), .col4(_3e5), .col5(_3e6), .col6(_3e7), .col7(_3e8),
    .col8(_3e9), .col9(_3e10), .col10(_3e11), .col11(_3e12), .col12(_3e13), .col13(_3e14), .col14(_3e15),
    .col15(_3e16));
  DotMatrix #(.matrixcols(16), .matrixrows(16)) dotmatrix_39 (
    .col0(_2e1), .col1(_2e2), .col2(_2e3), .col3(_2e4), .col4(_2e5), .col5(_2e6), .col6(_2e7), .col7(_2e8),
    .col8(_2e9), .col9(_2e10), .col10(_2e11), .col11(_2e12), .col12(_2e13), .col13(_2e14), .col14(_2e15),
    .col15(_2e16));
  DotMatrix #(.matrixcols(16), .matrixrows(16)) dotmatrix_40 (
    .col0(_1e1), .col1(_1e2), .col2(_1e3), .col3(_1e4), .col4(_1e5), .col5(_1e6), .col6(_1e7), .col7(_1e8),
    .col8(_1e9), .col9(_1e10), .col10(_1e11), .col11(_1e12), .col12(_1e13), .col13(_1e14), .col14(_1e15),
    .col15(_1e16));
  DotMatrix #(.matrixcols(16), .matrixrows(16)) dotmatrix_41 (
    .col0(_8f1), .col1(_8f2), .col2(_8f3), .col3(_8f4), .col4(_8f5), .col5(_8f6), .col6(_8f7), .col7(_8f8),
    .col8(_8f9), .col9(_8f10), .col10(_8f11), .col11(_8f12), .col12(_8f13), .col13(_8f14), .col14(_8f15),
    .col15(_8f16));
  DotMatrix #(.matrixcols(16), .matrixrows(16)) dotmatrix_42 (
    .col0(_7f1), .col1(_7f2), .col2(_7f3), .col3(_7f4), .col4(_7f5), .col5(_7f6), .col6(_7f7), .col7(_7f8),
    .col8(_7f9), .col9(_7f10), .col10(_7f11), .col11(_7f12), .col12(_7f13), .col13(_7f14), .col14(_7f15),
    .col15(_7f16));
  DotMatrix #(.matrixcols(16), .matrixrows(16)) dotmatrix_43 (
    .col0(_6f1), .col1(_6f2), .col2(_6f3), .col3(_6f4), .col4(_6f5), .col5(_6f6), .col6(_6f7), .col7(_6f8),
    .col8(_6f9), .col9(_6f10), .col10(_6f11), .col11(_6f12), .col12(_6f13), .col13(_6f14), .col14(_6f15),
    .col15(_6f16));
  DotMatrix #(.matrixcols(16), .matrixrows(16)) dotmatrix_44 (
    .col0(_5f1), .col1(_5f2), .col2(_5f3), .col3(_5f4), .col4(_5f5), .col5(_5f6), .col6(_5f7), .col7(_5f8),
    .col8(_5f9), .col9(_5f10), .col10(_5f11), .col11(_5f12), .col12(_5f13), .col13(_5f14), .col14(_5f15),
    .col15(_5f16));
  DotMatrix #(.matrixcols(16), .matrixrows(16)) dotmatrix_45 (
    .col0(_4f1), .col1(_4f2), .col2(_4f3), .col3(_4f4), .col4(_4f5), .col5(_4f6), .col6(_4f7), .col7(_4f8),
    .col8(_4f9), .col9(_4f10), .col10(_4f11), .col11(_4f12), .col12(_4f13), .col13(_4f14), .col14(_4f15),
    .col15(_4f16));
  DotMatrix #(.matrixcols(16), .matrixrows(16)) dotmatrix_46 (
    .col0(_3f1), .col1(_3f2), .col2(_3f3), .col3(_3f4), .col4(_3f5), .col5(_3f6), .col6(_3f7), .col7(_3f8),
    .col8(_3f9), .col9(_3f10), .col10(_3f11), .col11(_3f12), .col12(_3f13), .col13(_3f14), .col14(_3f15),
    .col15(_3f16));
  DotMatrix #(.matrixcols(16), .matrixrows(16)) dotmatrix_47 (
    .col0(_2f1), .col1(_2f2), .col2(_2f3), .col3(_2f4), .col4(_2f5), .col5(_2f6), .col6(_2f7), .col7(_2f8),
    .col8(_2f9), .col9(_2f10), .col10(_2f11), .col11(_2f12), .col12(_2f13), .col13(_2f14), .col14(_2f15),
    .col15(_2f16));
  DotMatrix #(.matrixcols(16), .matrixrows(16)) dotmatrix_48 (
    .col0(_1f1), .col1(_1f2), .col2(_1f3), .col3(_1f4), .col4(_1f5), .col5(_1f6), .col6(_1f7), .col7(_1f8),
    .col8(_1f9), .col9(_1f10), .col10(_1f11), .col11(_1f12), .col12(_1f13), .col13(_1f14), .col14(_1f15),
    .col15(_1f16));
  DotMatrix #(.matrixcols(16), .matrixrows(16)) dotmatrix_49 (
    .col0(_8g1), .col1(_8g2), .col2(_8g3), .col3(_8g4), .col4(_8g5), .col5(_8g6), .col6(_8g7), .col7(_8g8),
    .col8(_8g9), .col9(_8g10), .col10(_8g11), .col11(_8g12), .col12(_8g13), .col13(_8g14), .col14(_8g15),
    .col15(_8g16));
  DotMatrix #(.matrixcols(16), .matrixrows(16)) dotmatrix_50 (
    .col0(_7g1), .col1(_7g2), .col2(_7g3), .col3(_7g4), .col4(_7g5), .col5(_7g6), .col6(_7g7), .col7(_7g8),
    .col8(_7g9), .col9(_7g10), .col10(_7g11), .col11(_7g12), .col12(_7g13), .col13(_7g14), .col14(_7g15),
    .col15(_7g16));
  DotMatrix #(.matrixcols(16), .matrixrows(16)) dotmatrix_51 (
    .col0(_6g1), .col1(_6g2), .col2(_6g3), .col3(_6g4), .col4(_6g5), .col5(_6g6), .col6(_6g7), .col7(_6g8),
    .col8(_6g9), .col9(_6g10), .col10(_6g11), .col11(_6g12), .col12(_6g13), .col13(_6g14), .col14(_6g15),
    .col15(_6g16));
  DotMatrix #(.matrixcols(16), .matrixrows(16)) dotmatrix_52 (
    .col0(_5g1), .col1(_5g2), .col2(_5g3), .col3(_5g4), .col4(_5g5), .col5(_5g6), .col6(_5g7), .col7(_5g8),
    .col8(_5g9), .col9(_5g10), .col10(_5g11), .col11(_5g12), .col12(_5g13), .col13(_5g14), .col14(_5g15),
    .col15(_5g16));
  DotMatrix #(.matrixcols(16), .matrixrows(16)) dotmatrix_53 (
    .col0(_4g1), .col1(_4g2), .col2(_4g3), .col3(_4g4), .col4(_4g5), .col5(_4g6), .col6(_4g7), .col7(_4g8),
    .col8(_4g9), .col9(_4g10), .col10(_4g11), .col11(_4g12), .col12(_4g13), .col13(_4g14), .col14(_4g15),
    .col15(_4g16));
  DotMatrix #(.matrixcols(16), .matrixrows(16)) dotmatrix_54 (
    .col0(_3g1), .col1(_3g2), .col2(_3g3), .col3(_3g4), .col4(_3g5), .col5(_3g6), .col6(_3g7), .col7(_3g8),
    .col8(_3g9), .col9(_3g10), .col10(_3g11), .col11(_3g12), .col12(_3g13), .col13(_3g14), .col14(_3g15),
    .col15(_3g16));
  DotMatrix #(.matrixcols(16), .matrixrows(16)) dotmatrix_55 (
    .col0(_2g1), .col1(_2g2), .col2(_2g3), .col3(_2g4), .col4(_2g5), .col5(_2g6), .col6(_2g7), .col7(_2g8),
    .col8(_2g9), .col9(_2g10), .col10(_2g11), .col11(_2g12), .col12(_2g13), .col13(_2g14), .col14(_2g15),
    .col15(_2g16));
  DotMatrix #(.matrixcols(16), .matrixrows(16)) dotmatrix_56 (
    .col0(_1g1), .col1(_1g2), .col2(_1g3), .col3(_1g4), .col4(_1g5), .col5(_1g6), .col6(_1g7), .col7(_1g8),
    .col8(_1g9), .col9(_1g10), .col10(_1g11), .col11(_1g12), .col12(_1g13), .col13(_1g14), .col14(_1g15),
    .col15(_1g16));
  system_board system_board_1 ();  // open: stepIN, IOsignal, hold, clk, nothing, check, checkmate, stalemate, invalid, castling, step_inspected, stepOUT
  DotMatrix #(.matrixcols(16), .matrixrows(16)) dotmatrix_57 (
    .col0(_8h1), .col1(_8h2), .col2(_8h3), .col3(_8h4), .col4(_8h5), .col5(_8h6), .col6(_8h7), .col7(_8h8),
    .col8(_8h9), .col9(_8h10), .col10(_8h11), .col11(_8h12), .col12(_8h13), .col13(_8h14), .col14(_8h15),
    .col15(_8h16));
  DotMatrix #(.matrixcols(16), .matrixrows(16)) dotmatrix_58 (
    .col0(_7h1), .col1(_7h2), .col2(_7h3), .col3(_7h4), .col4(_7h5), .col5(_7h6), .col6(_7h7), .col7(_7h8),
    .col8(_7h9), .col9(_7h10), .col10(_7h11), .col11(_7h12), .col12(_7h13), .col13(_7h14), .col14(_7h15),
    .col15(_7h16));
  DotMatrix #(.matrixcols(16), .matrixrows(16)) dotmatrix_59 (
    .col0(_6h1), .col1(_6h2), .col2(_6h3), .col3(_6h4), .col4(_6h5), .col5(_6h6), .col6(_6h7), .col7(_6h8),
    .col8(_6h9), .col9(_6h10), .col10(_6h11), .col11(_6h12), .col12(_6h13), .col13(_6h14), .col14(_6h15),
    .col15(_6h16));
  DotMatrix #(.matrixcols(16), .matrixrows(16)) dotmatrix_60 (
    .col0(_5h1), .col1(_5h2), .col2(_5h3), .col3(_5h4), .col4(_5h5), .col5(_5h6), .col6(_5h7), .col7(_5h8),
    .col8(_5h9), .col9(_5h10), .col10(_5h11), .col11(_5h12), .col12(_5h13), .col13(_5h14), .col14(_5h15),
    .col15(_5h16));
  DotMatrix #(.matrixcols(16), .matrixrows(16)) dotmatrix_61 (
    .col0(_4h1), .col1(_4h2), .col2(_4h3), .col3(_4h4), .col4(_4h5), .col5(_4h6), .col6(_4h7), .col7(_4h8),
    .col8(_4h9), .col9(_4h10), .col10(_4h11), .col11(_4h12), .col12(_4h13), .col13(_4h14), .col14(_4h15),
    .col15(_4h16));
  DotMatrix #(.matrixcols(16), .matrixrows(16)) dotmatrix_62 (
    .col0(_3h1), .col1(_3h2), .col2(_3h3), .col3(_3h4), .col4(_3h5), .col5(_3h6), .col6(_3h7), .col7(_3h8),
    .col8(_3h9), .col9(_3h10), .col10(_3h11), .col11(_3h12), .col12(_3h13), .col13(_3h14), .col14(_3h15),
    .col15(_3h16));
  DotMatrix #(.matrixcols(16), .matrixrows(16)) dotmatrix_63 (
    .col0(_2h1), .col1(_2h2), .col2(_2h3), .col3(_2h4), .col4(_2h5), .col5(_2h6), .col6(_2h7), .col7(_2h8),
    .col8(_2h9), .col9(_2h10), .col10(_2h11), .col11(_2h12), .col12(_2h13), .col13(_2h14), .col14(_2h15),
    .col15(_2h16));
  DotMatrix #(.matrixcols(16), .matrixrows(16)) dotmatrix_64 (
    .col0(_1h1), .col1(_1h2), .col2(_1h3), .col3(_1h4), .col4(_1h5), .col5(_1h6), .col6(_1h7), .col7(_1h8),
    .col8(_1h9), .col9(_1h10), .col10(_1h11), .col11(_1h12), .col12(_1h13), .col13(_1h14), .col14(_1h15),
    .col15(_1h16));
  // Buffer buffer_1 is placed but not wired
  matrix matrix_1 (
    .column({16{1'b1}}), .column_1(_8a1), .column_2(_8a2), .column_3(_8a3), .column_4(_8a4), .column_5(_8a5),
    .column_6(_8a6), .column_7(_8a7), .column_8(_8a8), .column_9(_8a9), .column_10(_8a10), .column_11(_8a11),
    .column_12(_8a12), .column_13(_8a13), .column_14(_8a14), .column_15(_8a15), .column_16(_8a16),
    .change_matrix(_1), .clk(click), .current_column(matrix_1_current_column));
  matrix matrix_2 (
    .column({16{1'b1}}), .column_1(_7a1), .column_2(_7a2), .column_3(_7a3), .column_4(_7a4), .column_5(_7a5),
    .column_6(_7a6), .column_7(_7a7), .column_8(_7a8), .column_9(_7a9), .column_10(_7a10), .column_11(_7a11),
    .column_12(_7a12), .column_13(_7a13), .column_14(_7a14), .column_15(_7a15), .column_16(_7a16),
    .change_matrix(_9), .clk(click), .current_column(matrix_2_current_column));
  matrix matrix_3 (
    .column({16{1'b1}}), .column_1(_6a1), .column_2(_6a2), .column_3(_6a3), .column_4(_6a4), .column_5(_6a5),
    .column_6(_6a6), .column_7(_6a7), .column_8(_6a8), .column_9(_6a9), .column_10(_6a10), .column_11(_6a11),
    .column_12(_6a12), .column_13(_6a13), .column_14(_6a14), .column_15(_6a15), .column_16(_6a16),
    .change_matrix(_17), .clk(click), .current_column(matrix_3_current_column));
  matrix matrix_4 (
    .column({16{1'b1}}), .column_1(_5a1), .column_2(_5a2), .column_3(_5a3), .column_4(_5a4), .column_5(_5a5),
    .column_6(_5a6), .column_7(_5a7), .column_8(_5a8), .column_9(_5a9), .column_10(_5a10), .column_11(_5a11),
    .column_12(_5a12), .column_13(_5a13), .column_14(_5a14), .column_15(_5a15), .column_16(_5a16),
    .change_matrix(_25), .clk(click), .current_column(matrix_4_current_column));
  matrix matrix_5 (
    .column({16{1'b1}}), .column_1(_4a1), .column_2(_4a2), .column_3(_4a3), .column_4(_4a4), .column_5(_4a5),
    .column_6(_4a6), .column_7(_4a7), .column_8(_4a8), .column_9(_4a9), .column_10(_4a10), .column_11(_4a11),
    .column_12(_4a12), .column_13(_4a13), .column_14(_4a14), .column_15(_4a15), .column_16(_4a16),
    .change_matrix(_33), .clk(click), .current_column(matrix_5_current_column));
  matrix matrix_6 (
    .column({16{1'b1}}), .column_1(_3a1), .column_2(_3a2), .column_3(_3a3), .column_4(_3a4), .column_5(_3a5),
    .column_6(_3a6), .column_7(_3a7), .column_8(_3a8), .column_9(_3a9), .column_10(_3a10), .column_11(_3a11),
    .column_12(_3a12), .column_13(_3a13), .column_14(_3a14), .column_15(_3a15), .column_16(_3a16),
    .change_matrix(_41), .clk(click), .current_column(matrix_6_current_column));
  matrix matrix_7 (
    .column({16{1'b1}}), .column_1(_2a1), .column_2(_2a2), .column_3(_2a3), .column_4(_2a4), .column_5(_2a5),
    .column_6(_2a6), .column_7(_2a7), .column_8(_2a8), .column_9(_2a9), .column_10(_2a10), .column_11(_2a11),
    .column_12(_2a12), .column_13(_2a13), .column_14(_2a14), .column_15(_2a15), .column_16(_2a16),
    .change_matrix(_49), .clk(click), .current_column(matrix_7_current_column));
  matrix matrix_8 (
    .column({16{1'b1}}), .column_1(_1a1), .column_2(_1a2), .column_3(_1a3), .column_4(_1a4), .column_5(_1a5),
    .column_6(_1a6), .column_7(_1a7), .column_8(_1a8), .column_9(_1a9), .column_10(_1a10), .column_11(_1a11),
    .column_12(_1a12), .column_13(_1a13), .column_14(_1a14), .column_15(_1a15), .column_16(_1a16),
    .change_matrix(_57), .clk(click), .current_column(matrix_8_current_column));
  // Probe on matrix_1_current_column
  // Probe on matrix_2_current_column
  // Probe on matrix_3_current_column
  // Probe on matrix_4_current_column
  // Probe on matrix_5_current_column
  // Probe on matrix_6_current_column
  // Probe on matrix_7_current_column
  // Probe on matrix_8_current_column
  select_matrix select_matrix_1 (
    .bus_0(bus_0), .out_18(_1), .out_2(_2), .out_50(_33), .out_19(_3), .out_34(_34), .out_3(_4),
    .out_51(_35), .out_20(_5), .out_35(_36), .out_4(_6), .out_52(_37), .out_21(_7), .out_36(_38), .out_5(_8),
    .out_53(_39), .out_22(_9), .out_37(_40), .out_6(_10), .out_54(_41), .out_23(_11), .out_38(_42),
    .out_7(_12), .out_55(_43), .out_24(_13), .out_39(_44), .out_8(_14), .out_56(_45), .out_25(_15),
    .out_40(_46), .out_9(_16), .out_57(_47), .out_26(_17), .out_41(_48), .out_10(_18), .out_58(_49),
    .out_27(_19), .out_42(_50), .out_11(_20), .out_59(_51), .out_28(_21), .out_43(_52), .out_12(_22),
    .out_60(_53), .out_29(_23), .out_44(_54), .out_13(_24), .out_61(_55), .out_30(_25), .out_45(_56),
    .out_14(_26), .out_62(_57), .out_31(_27), .out_46(_58), .out_15(_28), .out_63(_59), .out_32(_29),
    .out_47(_60), .out_16(_30), .out_64(_61), .out_33(_31), .out_48(_62), .out_17(_32), .out_65(_63),
    .out_49(_64));
  matrix matrix_9 (
    .column({16{1'b1}}), .column_1(_8b1), .column_2(_8b2), .column_3(_8b3), .column_4(_8b4), .column_5(_8b5),
    .column_6(_8b6), .column_7(_8b7), .column_8(_8b8), .column_9(_8b9), .column_10(_8b10), .column_11(_8b11),
    .column_12(_8b12), .column_13(_8b13), .column_14(_8b14), .column_15(_8b15), .column_16(_8b16),
    .change_matrix(_2), .clk(click), .current_column(matrix_9_current_column));
  matrix matrix_10 (
    .column({16{1'b1}}), .column_1(_7b1), .column_2(_7b2), .column_3(_7b3), .column_4(_7b4), .column_5(_7b5),
    .column_6(_7b6), .column_7(_7b7), .column_8(_7b8), .column_9(_7b9), .column_10(_7b10), .column_11(_7b11),
    .column_12(_7b12), .column_13(_7b13), .column_14(_7b14), .column_15(_7b15), .column_16(_7b16),
    .change_matrix(_10), .clk(click), .current_column(matrix_10_current_column));
  matrix matrix_11 (
    .column({16{1'b1}}), .column_1(_6b1), .column_2(_6b2), .column_3(_6b3), .column_4(_6b4), .column_5(_6b5),
    .column_6(_6b6), .column_7(_6b7), .column_8(_6b8), .column_9(_6b9), .column_10(_6b10), .column_11(_6b11),
    .column_12(_6b12), .column_13(_6b13), .column_14(_6b14), .column_15(_6b15), .column_16(_6b16),
    .change_matrix(_18), .clk(click), .current_column(matrix_11_current_column));
  matrix matrix_12 (
    .column({16{1'b1}}), .column_1(_5b1), .column_2(_5b2), .column_3(_5b3), .column_4(_5b4), .column_5(_5b5),
    .column_6(_5b6), .column_7(_5b7), .column_8(_5b8), .column_9(_5b9), .column_10(_5b10), .column_11(_5b11),
    .column_12(_5b12), .column_13(_5b13), .column_14(_5b14), .column_15(_5b15), .column_16(_5b16),
    .change_matrix(_26), .clk(click), .current_column(matrix_12_current_column));
  matrix matrix_13 (
    .column({16{1'b1}}), .column_1(_4b1), .column_2(_4b2), .column_3(_4b3), .column_4(_4b4), .column_5(_4b5),
    .column_6(_4b6), .column_7(_4b7), .column_8(_4b8), .column_9(_4b9), .column_10(_4b10), .column_11(_4b11),
    .column_12(_4b12), .column_13(_4b13), .column_14(_4b14), .column_15(_4b15), .column_16(_4b16),
    .change_matrix(_34), .clk(click), .current_column(matrix_13_current_column));
  matrix matrix_14 (
    .column({16{1'b1}}), .column_1(_3b1), .column_2(_3b2), .column_3(_3b3), .column_4(_3b4), .column_5(_3b5),
    .column_6(_3b6), .column_7(_3b7), .column_8(_3b8), .column_9(_3b9), .column_10(_3b10), .column_11(_3b11),
    .column_12(_3b12), .column_13(_3b13), .column_14(_3b14), .column_15(_3b15), .column_16(_3b16),
    .change_matrix(_42), .clk(click), .current_column(matrix_14_current_column));
  matrix matrix_15 (
    .column({16{1'b1}}), .column_1(_2b1), .column_2(_2b2), .column_3(_2b3), .column_4(_2b4), .column_5(_2b5),
    .column_6(_2b6), .column_7(_2b7), .column_8(_2b8), .column_9(_2b9), .column_10(_2b10), .column_11(_2b11),
    .column_12(_2b12), .column_13(_2b13), .column_14(_2b14), .column_15(_2b15), .column_16(_2b16),
    .change_matrix(_50), .clk(click), .current_column(matrix_15_current_column));
  matrix matrix_16 (
    .column({16{1'b1}}), .column_1(_1b1), .column_2(_1b2), .column_3(_1b3), .column_4(_1b4), .column_5(_1b5),
    .column_6(_1b6), .column_7(_1b7), .column_8(_1b8), .column_9(_1b9), .column_10(_1b10), .column_11(_1b11),
    .column_12(_1b12), .column_13(_1b13), .column_14(_1b14), .column_15(_1b15), .column_16(_1b16),
    .change_matrix(_58), .clk(click), .current_column(matrix_16_current_column));
  // Probe on matrix_9_current_column
  // Probe on matrix_10_current_column
  // Probe on matrix_11_current_column
  // Probe on matrix_12_current_column
  // Probe on matrix_13_current_column
  // Probe on matrix_14_current_column
  // Probe on matrix_15_current_column
  // Probe on matrix_16_current_column
  matrix matrix_17 (
    .column({16{1'b1}}), .column_1(_8c1), .column_2(_8c2), .column_3(_8c3), .column_4(_8c4), .column_5(_8c5),
    .column_6(_8c6), .column_7(_8c7), .column_8(_8c8), .column_9(_8c9), .column_10(_8c10), .column_11(_8c11),
    .column_12(_8c12), .column_13(_8c13), .column_14(_8c14), .column_15(_8c15), .column_16(_8c16),
    .change_matrix(_3), .clk(click), .current_column(matrix_17_current_column));
  matrix matrix_18 (
    .column({16{1'b1}}), .column_1(_7c1), .column_2(_7c2), .column_3(_7c3), .column_4(_7c4), .column_5(_7c5),
    .column_6(_7c6), .column_7(_7c7), .column_8(_7c8), .column_9(_7c9), .column_10(_7c10), .column_11(_7c11),
    .column_12(_7c12), .column_13(_7c13), .column_14(_7c14), .column_15(_7c15), .column_16(_7c16),
    .change_matrix(_11), .clk(click), .current_column(matrix_18_current_column));
  matrix matrix_19 (
    .column({16{1'b1}}), .column_1(_6c1), .column_2(_6c2), .column_3(_6c3), .column_4(_6c4), .column_5(_6c5),
    .column_6(_6c6), .column_7(_6c7), .column_8(_6c8), .column_9(_6c9), .column_10(_6c10), .column_11(_6c11),
    .column_12(_6c12), .column_13(_6c13), .column_14(_6c14), .column_15(_6c15), .column_16(_6c16),
    .change_matrix(_19), .clk(click), .current_column(matrix_19_current_column));
  matrix matrix_20 (
    .column({16{1'b1}}), .column_1(_5c1), .column_2(_5c2), .column_3(_5c3), .column_4(_5c4), .column_5(_5c5),
    .column_6(_5c6), .column_7(_5c7), .column_8(_5c8), .column_9(_5c9), .column_10(_5c10), .column_11(_5c11),
    .column_12(_5c12), .column_13(_5c13), .column_14(_5c14), .column_15(_5c15), .column_16(_5c16),
    .change_matrix(_27), .clk(click), .current_column(matrix_20_current_column));
  matrix matrix_21 (
    .column({16{1'b1}}), .column_1(_4c1), .column_2(_4c2), .column_3(_4c3), .column_4(_4c4), .column_5(_4c5),
    .column_6(_4c6), .column_7(_4c7), .column_8(_4c8), .column_9(_4c9), .column_10(_4c10), .column_11(_4c11),
    .column_12(_4c12), .column_13(_4c13), .column_14(_4c14), .column_15(_4c15), .column_16(_4c16),
    .change_matrix(_35), .clk(click), .current_column(matrix_21_current_column));
  matrix matrix_22 (
    .column({16{1'b1}}), .column_1(_3c1), .column_2(_3c2), .column_3(_3c3), .column_4(_3c4), .column_5(_3c5),
    .column_6(_3c6), .column_7(_3c7), .column_8(_3c8), .column_9(_3c9), .column_10(_3c10), .column_11(_3c11),
    .column_12(_3c12), .column_13(_3c13), .column_14(_3c14), .column_15(_3c15), .column_16(_3c16),
    .change_matrix(_43), .clk(click), .current_column(matrix_22_current_column));
  matrix matrix_23 (
    .column({16{1'b1}}), .column_1(_2c1), .column_2(_2c2), .column_3(_2c3), .column_4(_2c4), .column_5(_2c5),
    .column_6(_2c6), .column_7(_2c7), .column_8(_2c8), .column_9(_2c9), .column_10(_2c10), .column_11(_2c11),
    .column_12(_2c12), .column_13(_2c13), .column_14(_2c14), .column_15(_2c15), .column_16(_2c16),
    .change_matrix(_51), .clk(click), .current_column(matrix_23_current_column));
  matrix matrix_24 (
    .column({16{1'b1}}), .column_1(_1c1), .column_2(_1c2), .column_3(_1c3), .column_4(_1c4), .column_5(_1c5),
    .column_6(_1c6), .column_7(_1c7), .column_8(_1c8), .column_9(_1c9), .column_10(_1c10), .column_11(_1c11),
    .column_12(_1c12), .column_13(_1c13), .column_14(_1c14), .column_15(_1c15), .column_16(_1c16),
    .change_matrix(_59), .clk(click), .current_column(matrix_24_current_column));
  // Probe on matrix_17_current_column
  // Probe on matrix_18_current_column
  // Probe on matrix_19_current_column
  // Probe on matrix_20_current_column
  // Probe on matrix_21_current_column
  // Probe on matrix_22_current_column
  // Probe on matrix_23_current_column
  // Probe on matrix_24_current_column
  matrix matrix_25 (
    .column({16{1'b1}}), .column_1(_8d1), .column_2(_8d2), .column_3(_8d3), .column_4(_8d4), .column_5(_8d5),
    .column_6(_8d6), .column_7(_8d7), .column_8(_8d8), .column_9(_8d9), .column_10(_8d10), .column_11(_8d11),
    .column_12(_8d12), .column_13(_8d13), .column_14(_8d14), .column_15(_8d15), .column_16(_8d16),
    .change_matrix(_4), .clk(click), .current_column(matrix_25_current_column));
  matrix matrix_26 (
    .column({16{1'b1}}), .column_1(_7d1), .column_2(_7d2), .column_3(_7d3), .column_4(_7d4), .column_5(_7d5),
    .column_6(_7d6), .column_7(_7d7), .column_8(_7d8), .column_9(_7d9), .column_10(_7d10), .column_11(_7d11),
    .column_12(_7d12), .column_13(_7d13), .column_14(_7d14), .column_15(_7d15), .column_16(_7d16),
    .change_matrix(_12), .clk(click), .current_column(matrix_26_current_column));
  matrix matrix_27 (
    .column({16{1'b1}}), .column_1(_6d1), .column_2(_6d2), .column_3(_6d3), .column_4(_6d4), .column_5(_6d5),
    .column_6(_6d6), .column_7(_6d7), .column_8(_6d8), .column_9(_6d9), .column_10(_6d10), .column_11(_6d11),
    .column_12(_6d12), .column_13(_6d13), .column_14(_6d14), .column_15(_6d15), .column_16(_6d16),
    .change_matrix(_20), .clk(click), .current_column(matrix_27_current_column));
  matrix matrix_28 (
    .column({16{1'b1}}), .column_1(_5d1), .column_2(_5d2), .column_3(_5d3), .column_4(_5d4), .column_5(_5d5),
    .column_6(_5d6), .column_7(_5d7), .column_8(_5d8), .column_9(_5d9), .column_10(_5d10), .column_11(_5d11),
    .column_12(_5d12), .column_13(_5d13), .column_14(_5d14), .column_15(_5d15), .column_16(_5d16),
    .change_matrix(_28), .clk(click), .current_column(matrix_28_current_column));
  matrix matrix_29 (
    .column({16{1'b1}}), .column_1(_4d1), .column_2(_4d2), .column_3(_4d3), .column_4(_4d4), .column_5(_4d5),
    .column_6(_4d6), .column_7(_4d7), .column_8(_4d8), .column_9(_4d9), .column_10(_4d10), .column_11(_4d11),
    .column_12(_4d12), .column_13(_4d13), .column_14(_4d14), .column_15(_4d15), .column_16(_4d16),
    .change_matrix(_36), .clk(click), .current_column(matrix_29_current_column));
  matrix matrix_30 (
    .column({16{1'b1}}), .column_1(_3d1), .column_2(_3d2), .column_3(_3d3), .column_4(_3d4), .column_5(_3d5),
    .column_6(_3d6), .column_7(_3d7), .column_8(_3d8), .column_9(_3d9), .column_10(_3d10), .column_11(_3d11),
    .column_12(_3d12), .column_13(_3d13), .column_14(_3d14), .column_15(_3d15), .column_16(_3d16),
    .change_matrix(_44), .clk(click), .current_column(matrix_30_current_column));
  matrix matrix_31 (
    .column({16{1'b1}}), .column_1(_2d1), .column_2(_2d2), .column_3(_2d3), .column_4(_2d4), .column_5(_2d5),
    .column_6(_2d6), .column_7(_2d7), .column_8(_2d8), .column_9(_2d9), .column_10(_2d10), .column_11(_2d11),
    .column_12(_2d12), .column_13(_2d13), .column_14(_2d14), .column_15(_2d15), .column_16(_2d16),
    .change_matrix(_52), .clk(click), .current_column(matrix_31_current_column));
  matrix matrix_32 (
    .column({16{1'b1}}), .column_1(_1d1), .column_2(_1d2), .column_3(_1d3), .column_4(_1d4), .column_5(_1d5),
    .column_6(_1d6), .column_7(_1d7), .column_8(_1d8), .column_9(_1d9), .column_10(_1d10), .column_11(_1d11),
    .column_12(_1d12), .column_13(_1d13), .column_14(_1d14), .column_15(_1d15), .column_16(_1d16),
    .change_matrix(_60), .clk(click), .current_column(matrix_32_current_column));
  // Probe on matrix_25_current_column
  // Probe on matrix_26_current_column
  // Probe on matrix_27_current_column
  // Probe on matrix_28_current_column
  // Probe on matrix_29_current_column
  // Probe on matrix_30_current_column
  // Probe on matrix_31_current_column
  // Probe on matrix_32_current_column
  matrix matrix_33 (
    .column({16{1'b1}}), .column_1(_8e1), .column_2(_8e2), .column_3(_8e3), .column_4(_8e4), .column_5(_8e5),
    .column_6(_8e6), .column_7(_8e7), .column_8(_8e8), .column_9(_8e9), .column_10(_8e10), .column_11(_8e11),
    .column_12(_8e12), .column_13(_8e13), .column_14(_8e14), .column_15(_8e15), .column_16(_8e16),
    .change_matrix(_5), .clk(click), .current_column(matrix_33_current_column));
  matrix matrix_34 (
    .column({16{1'b1}}), .column_1(_7e1), .column_2(_7e2), .column_3(_7e3), .column_4(_7e4), .column_5(_7e5),
    .column_6(_7e6), .column_7(_7e7), .column_8(_7e8), .column_9(_7e9), .column_10(_7e10), .column_11(_7e11),
    .column_12(_7e12), .column_13(_7e13), .column_14(_7e14), .column_15(_7e15), .column_16(_7e16),
    .change_matrix(_13), .clk(click), .current_column(matrix_34_current_column));
  matrix matrix_35 (
    .column({16{1'b1}}), .column_1(_6e1), .column_2(_6e2), .column_3(_6e3), .column_4(_6e4), .column_5(_6e5),
    .column_6(_6e6), .column_7(_6e7), .column_8(_6e8), .column_9(_6e9), .column_10(_6e10), .column_11(_6e11),
    .column_12(_6e12), .column_13(_6e13), .column_14(_6e14), .column_15(_6e15), .column_16(_6e16),
    .change_matrix(_21), .clk(click), .current_column(matrix_35_current_column));
  matrix matrix_36 (
    .column({16{1'b1}}), .column_1(_5e1), .column_2(_5e2), .column_3(_5e3), .column_4(_5e4), .column_5(_5e5),
    .column_6(_5e6), .column_7(_5e7), .column_8(_5e8), .column_9(_5e9), .column_10(_5e10), .column_11(_5e11),
    .column_12(_5e12), .column_13(_5e13), .column_14(_5e14), .column_15(_5e15), .column_16(_5e16),
    .change_matrix(_29), .clk(click), .current_column(matrix_36_current_column));
  matrix matrix_37 (
    .column({16{1'b1}}), .column_1(_4e1), .column_2(_4e2), .column_3(_4e3), .column_4(_4e4), .column_5(_4e5),
    .column_6(_4e6), .column_7(_4e7), .column_8(_4e8), .column_9(_4e9), .column_10(_4e10), .column_11(_4e11),
    .column_12(_4e12), .column_13(_4e13), .column_14(_4e14), .column_15(_4e15), .column_16(_4e16),
    .change_matrix(_37), .clk(click), .current_column(matrix_37_current_column));
  matrix matrix_38 (
    .column({16{1'b1}}), .column_1(_3e1), .column_2(_3e2), .column_3(_3e3), .column_4(_3e4), .column_5(_3e5),
    .column_6(_3e6), .column_7(_3e7), .column_8(_3e8), .column_9(_3e9), .column_10(_3e10), .column_11(_3e11),
    .column_12(_3e12), .column_13(_3e13), .column_14(_3e14), .column_15(_3e15), .column_16(_3e16),
    .change_matrix(_45), .clk(click), .current_column(matrix_38_current_column));
  matrix matrix_39 (
    .column({16{1'b1}}), .column_1(_2e1), .column_2(_2e2), .column_3(_2e3), .column_4(_2e4), .column_5(_2e5),
    .column_6(_2e6), .column_7(_2e7), .column_8(_2e8), .column_9(_2e9), .column_10(_2e10), .column_11(_2e11),
    .column_12(_2e12), .column_13(_2e13), .column_14(_2e14), .column_15(_2e15), .column_16(_2e16),
    .change_matrix(_53), .clk(click), .current_column(matrix_39_current_column));
  matrix matrix_40 (
    .column({16{1'b1}}), .column_1(_1e1), .column_2(_1e2), .column_3(_1e3), .column_4(_1e4), .column_5(_1e5),
    .column_6(_1e6), .column_7(_1e7), .column_8(_1e8), .column_9(_1e9), .column_10(_1e10), .column_11(_1e11),
    .column_12(_1e12), .column_13(_1e13), .column_14(_1e14), .column_15(_1e15), .column_16(_1e16),
    .change_matrix(_61), .clk(click), .current_column(matrix_40_current_column));
  // Probe on matrix_33_current_column
  // Probe on matrix_34_current_column
  // Probe on matrix_35_current_column
  // Probe on matrix_36_current_column
  // Probe on matrix_37_current_column
  // Probe on matrix_38_current_column
  // Probe on matrix_39_current_column
  // Probe on matrix_40_current_column
  matrix matrix_41 (
    .column({16{1'b1}}), .column_1(_8f1), .column_2(_8f2), .column_3(_8f3), .column_4(_8f4), .column_5(_8f5),
    .column_6(_8f6), .column_7(_8f7), .column_8(_8f8), .column_9(_8f9), .column_10(_8f10), .column_11(_8f11),
    .column_12(_8f12), .column_13(_8f13), .column_14(_8f14), .column_15(_8f15), .column_16(_8f16),
    .change_matrix(_6), .clk(click), .current_column(matrix_41_current_column));
  matrix matrix_42 (
    .column({16{1'b1}}), .column_1(_7f1), .column_2(_7f2), .column_3(_7f3), .column_4(_7f4), .column_5(_7f5),
    .column_6(_7f6), .column_7(_7f7), .column_8(_7f8), .column_9(_7f9), .column_10(_7f10), .column_11(_7f11),
    .column_12(_7f12), .column_13(_7f13), .column_14(_7f14), .column_15(_7f15), .column_16(_7f16),
    .change_matrix(_14), .clk(click), .current_column(matrix_42_current_column));
  matrix matrix_43 (
    .column({16{1'b1}}), .column_1(_6f1), .column_2(_6f2), .column_3(_6f3), .column_4(_6f4), .column_5(_6f5),
    .column_6(_6f6), .column_7(_6f7), .column_8(_6f8), .column_9(_6f9), .column_10(_6f10), .column_11(_6f11),
    .column_12(_6f12), .column_13(_6f13), .column_14(_6f14), .column_15(_6f15), .column_16(_6f16),
    .change_matrix(_22), .clk(click), .current_column(matrix_43_current_column));
  matrix matrix_44 (
    .column({16{1'b1}}), .column_1(_5f1), .column_2(_5f2), .column_3(_5f3), .column_4(_5f4), .column_5(_5f5),
    .column_6(_5f6), .column_7(_5f7), .column_8(_5f8), .column_9(_5f9), .column_10(_5f10), .column_11(_5f11),
    .column_12(_5f12), .column_13(_5f13), .column_14(_5f14), .column_15(_5f15), .column_16(_5f16),
    .change_matrix(_30), .clk(click), .current_column(matrix_44_current_column));
  matrix matrix_45 (
    .column({16{1'b1}}), .column_1(_4f1), .column_2(_4f2), .column_3(_4f3), .column_4(_4f4), .column_5(_4f5),
    .column_6(_4f6), .column_7(_4f7), .column_8(_4f8), .column_9(_4f9), .column_10(_4f10), .column_11(_4f11),
    .column_12(_4f12), .column_13(_4f13), .column_14(_4f14), .column_15(_4f15), .column_16(_4f16),
    .change_matrix(_38), .clk(click), .current_column(matrix_45_current_column));
  matrix matrix_46 (
    .column({16{1'b1}}), .column_1(_3f1), .column_2(_3f2), .column_3(_3f3), .column_4(_3f4), .column_5(_3f5),
    .column_6(_3f6), .column_7(_3f7), .column_8(_3f8), .column_9(_3f9), .column_10(_3f10), .column_11(_3f11),
    .column_12(_3f12), .column_13(_3f13), .column_14(_3f14), .column_15(_3f15), .column_16(_3f16),
    .change_matrix(_46), .clk(click), .current_column(matrix_46_current_column));
  matrix matrix_47 (
    .column({16{1'b1}}), .column_1(_2f1), .column_2(_2f2), .column_3(_2f3), .column_4(_2f4), .column_5(_2f5),
    .column_6(_2f6), .column_7(_2f7), .column_8(_2f8), .column_9(_2f9), .column_10(_2f10), .column_11(_2f11),
    .column_12(_2f12), .column_13(_2f13), .column_14(_2f14), .column_15(_2f15), .column_16(_2f16),
    .change_matrix(_54), .clk(click), .current_column(matrix_47_current_column));
  matrix matrix_48 (
    .column({16{1'b1}}), .column_1(_1f1), .column_2(_1f2), .column_3(_1f3), .column_4(_1f4), .column_5(_1f5),
    .column_6(_1f6), .column_7(_1f7), .column_8(_1f8), .column_9(_1f9), .column_10(_1f10), .column_11(_1f11),
    .column_12(_1f12), .column_13(_1f13), .column_14(_1f14), .column_15(_1f15), .column_16(_1f16),
    .change_matrix(_62), .clk(click), .current_column(matrix_48_current_column));
  // Probe on matrix_41_current_column
  // Probe on matrix_42_current_column
  // Probe on matrix_43_current_column
  // Probe on matrix_44_current_column
  // Probe on matrix_45_current_column
  // Probe on matrix_46_current_column
  // Probe on matrix_47_current_column
  // Probe on matrix_48_current_column
  matrix matrix_49 (
    .column({16{1'b1}}), .column_1(_8g1), .column_2(_8g2), .column_3(_8g3), .column_4(_8g4), .column_5(_8g5),
    .column_6(_8g6), .column_7(_8g7), .column_8(_8g8), .column_9(_8g9), .column_10(_8g10), .column_11(_8g11),
    .column_12(_8g12), .column_13(_8g13), .column_14(_8g14), .column_15(_8g15), .column_16(_8g16),
    .change_matrix(_7), .clk(click), .current_column(matrix_49_current_column));
  matrix matrix_50 (
    .column({16{1'b1}}), .column_1(_7g1), .column_2(_7g2), .column_3(_7g3), .column_4(_7g4), .column_5(_7g5),
    .column_6(_7g6), .column_7(_7g7), .column_8(_7g8), .column_9(_7g9), .column_10(_7g10), .column_11(_7g11),
    .column_12(_7g12), .column_13(_7g13), .column_14(_7g14), .column_15(_7g15), .column_16(_7g16),
    .change_matrix(_15), .clk(click), .current_column(matrix_50_current_column));
  matrix matrix_51 (
    .column({16{1'b1}}), .column_1(_6g1), .column_2(_6g2), .column_3(_6g3), .column_4(_6g4), .column_5(_6g5),
    .column_6(_6g6), .column_7(_6g7), .column_8(_6g8), .column_9(_6g9), .column_10(_6g10), .column_11(_6g11),
    .column_12(_6g12), .column_13(_6g13), .column_14(_6g14), .column_15(_6g15), .column_16(_6g16),
    .change_matrix(_23), .clk(click), .current_column(matrix_51_current_column));
  matrix matrix_52 (
    .column({16{1'b1}}), .column_1(_5g1), .column_2(_5g2), .column_3(_5g3), .column_4(_5g4), .column_5(_5g5),
    .column_6(_5g6), .column_7(_5g7), .column_8(_5g8), .column_9(_5g9), .column_10(_5g10), .column_11(_5g11),
    .column_12(_5g12), .column_13(_5g13), .column_14(_5g14), .column_15(_5g15), .column_16(_5g16),
    .change_matrix(_31), .clk(click), .current_column(matrix_52_current_column));
  matrix matrix_53 (
    .column({16{1'b1}}), .column_1(_4g1), .column_2(_4g2), .column_3(_4g3), .column_4(_4g4), .column_5(_4g5),
    .column_6(_4g6), .column_7(_4g7), .column_8(_4g8), .column_9(_4g9), .column_10(_4g10), .column_11(_4g11),
    .column_12(_4g12), .column_13(_4g13), .column_14(_4g14), .column_15(_4g15), .column_16(_4g16),
    .change_matrix(_39), .clk(click), .current_column(matrix_53_current_column));
  matrix matrix_54 (
    .column({16{1'b1}}), .column_1(_3g1), .column_2(_3g2), .column_3(_3g3), .column_4(_3g4), .column_5(_3g5),
    .column_6(_3g6), .column_7(_3g7), .column_8(_3g8), .column_9(_3g9), .column_10(_3g10), .column_11(_3g11),
    .column_12(_3g12), .column_13(_3g13), .column_14(_3g14), .column_15(_3g15), .column_16(_3g16),
    .change_matrix(_47), .clk(click), .current_column(matrix_54_current_column));
  matrix matrix_55 (
    .column({16{1'b1}}), .column_1(_2g1), .column_2(_2g2), .column_3(_2g3), .column_4(_2g4), .column_5(_2g5),
    .column_6(_2g6), .column_7(_2g7), .column_8(_2g8), .column_9(_2g9), .column_10(_2g10), .column_11(_2g11),
    .column_12(_2g12), .column_13(_2g13), .column_14(_2g14), .column_15(_2g15), .column_16(_2g16),
    .change_matrix(_55), .clk(click), .current_column(matrix_55_current_column));
  matrix matrix_56 (
    .column({16{1'b1}}), .column_1(_1g1), .column_2(_1g2), .column_3(_1g3), .column_4(_1g4), .column_5(_1g5),
    .column_6(_1g6), .column_7(_1g7), .column_8(_1g8), .column_9(_1g9), .column_10(_1g10), .column_11(_1g11),
    .column_12(_1g12), .column_13(_1g13), .column_14(_1g14), .column_15(_1g15), .column_16(_1g16),
    .change_matrix(_63), .clk(click), .current_column(matrix_56_current_column));
  // Probe on matrix_49_current_column
  // Probe on matrix_50_current_column
  // Probe on matrix_51_current_column
  // Probe on matrix_52_current_column
  // Probe on matrix_53_current_column
  // Probe on matrix_54_current_column
  // Probe on matrix_55_current_column
  // Probe on matrix_56_current_column
  matrix matrix_57 (
    .column({16{1'b1}}), .column_1(_8h1), .column_2(_8h2), .column_3(_8h3), .column_4(_8h4), .column_5(_8h5),
    .column_6(_8h6), .column_7(_8h7), .column_8(_8h8), .column_9(_8h9), .column_10(_8h10), .column_11(_8h11),
    .column_12(_8h12), .column_13(_8h13), .column_14(_8h14), .column_15(_8h15), .column_16(_8h16),
    .change_matrix(_8), .clk(click), .current_column(matrix_57_current_column));
  matrix matrix_58 (
    .column({16{1'b1}}), .column_1(_7h1), .column_2(_7h2), .column_3(_7h3), .column_4(_7h4), .column_5(_7h5),
    .column_6(_7h6), .column_7(_7h7), .column_8(_7h8), .column_9(_7h9), .column_10(_7h10), .column_11(_7h11),
    .column_12(_7h12), .column_13(_7h13), .column_14(_7h14), .column_15(_7h15), .column_16(_7h16),
    .change_matrix(_16), .clk(click), .current_column(matrix_58_current_column));
  matrix matrix_59 (
    .column({16{1'b1}}), .column_1(_6h1), .column_2(_6h2), .column_3(_6h3), .column_4(_6h4), .column_5(_6h5),
    .column_6(_6h6), .column_7(_6h7), .column_8(_6h8), .column_9(_6h9), .column_10(_6h10), .column_11(_6h11),
    .column_12(_6h12), .column_13(_6h13), .column_14(_6h14), .column_15(_6h15), .column_16(_6h16),
    .change_matrix(_24), .clk(click), .current_column(matrix_59_current_column));
  matrix matrix_60 (
    .column({16{1'b1}}), .column_1(_5h1), .column_2(_5h2), .column_3(_5h3), .column_4(_5h4), .column_5(_5h5),
    .column_6(_5h6), .column_7(_5h7), .column_8(_5h8), .column_9(_5h9), .column_10(_5h10), .column_11(_5h11),
    .column_12(_5h12), .column_13(_5h13), .column_14(_5h14), .column_15(_5h15), .column_16(_5h16),
    .change_matrix(_32), .clk(click), .current_column(matrix_60_current_column));
  matrix matrix_61 (
    .column({16{1'b1}}), .column_1(_4h1), .column_2(_4h2), .column_3(_4h3), .column_4(_4h4), .column_5(_4h5),
    .column_6(_4h6), .column_7(_4h7), .column_8(_4h8), .column_9(_4h9), .column_10(_4h10), .column_11(_4h11),
    .column_12(_4h12), .column_13(_4h13), .column_14(_4h14), .column_15(_4h15), .column_16(_4h16),
    .change_matrix(_40), .clk(click), .current_column(matrix_61_current_column));
  matrix matrix_62 (
    .column({16{1'b1}}), .column_1(_3h1), .column_2(_3h2), .column_3(_3h3), .column_4(_3h4), .column_5(_3h5),
    .column_6(_3h6), .column_7(_3h7), .column_8(_3h8), .column_9(_3h9), .column_10(_3h10), .column_11(_3h11),
    .column_12(_3h12), .column_13(_3h13), .column_14(_3h14), .column_15(_3h15), .column_16(_3h16),
    .change_matrix(_48), .clk(click), .current_column(matrix_62_current_column));
  matrix matrix_63 (
    .column({16{1'b1}}), .column_1(_2h1), .column_2(_2h2), .column_3(_2h3), .column_4(_2h4), .column_5(_2h5),
    .column_6(_2h6), .column_7(_2h7), .column_8(_2h8), .column_9(_2h9), .column_10(_2h10), .column_11(_2h11),
    .column_12(_2h12), .column_13(_2h13), .column_14(_2h14), .column_15(_2h15), .column_16(_2h16),
    .change_matrix(_56), .clk(click), .current_column(matrix_63_current_column));
  matrix matrix_64 (
    .column({16{1'b1}}), .column_1(_1h1), .column_2(_1h2), .column_3(_1h3), .column_4(_1h4), .column_5(_1h5),
    .column_6(_1h6), .column_7(_1h7), .column_8(_1h8), .column_9(_1h9), .column_10(_1h10), .column_11(_1h11),
    .column_12(_1h12), .column_13(_1h13), .column_14(_1h14), .column_15(_1h15), .column_16(_1h16),
    .change_matrix(_64), .clk(click), .current_column(matrix_64_current_column));
  // Probe on matrix_57_current_column
  // Probe on matrix_58_current_column
  // Probe on matrix_59_current_column
  // Probe on matrix_60_current_column
  // Probe on matrix_61_current_column
  // Probe on matrix_62_current_column
  // Probe on matrix_63_current_column
  // Probe on matrix_64_current_column

  // Other names for the same wires on the sheet: tact = click
endmodule

module asset_memory (
  input  [15:0] addr,
  input  [15:0] column,
  input  clock,
  input  \end 
);
endmodule

module matrix (
  input  [15:0] column,
  input  clk,
  input  change_matrix,
  output [15:0] column_2,
  output [15:0] column_4,
  output [15:0] column_6,
  output [15:0] column_8,
  output [15:0] column_10,
  output [15:0] column_12,
  output [15:0] column_14,
  output [15:0] column_16,
  output [15:0] column_1,
  output [15:0] column_3,
  output [15:0] column_5,
  output [15:0] column_7,
  output [15:0] column_9,
  output [15:0] column_11,
  output [15:0] column_13,
  output [15:0] column_15,
  output [3:0] current_column
);

  wire and_1_out, comparator_1_gt, decoder_1_out0, decoder_1_out1, decoder_1_out2, decoder_1_out3,
       decoder_1_out4, decoder_1_out5, decoder_1_out6, decoder_1_out7, decoder_1_out8, decoder_1_out9,
       decoder_1_out10, decoder_1_out11, decoder_1_out12, decoder_1_out13, decoder_1_out14, decoder_1_out15;
  wire [3:0] adder_1_out;

  Register #(.width(4)) register_1 (
    .D(adder_1_out), .Q(current_column), .clk(and_1_out), .clr(comparator_1_gt));  // open: en
  Adder #(.width(4)) adder_1 (.a(4'b0001), .b(current_column), .out(adder_1_out));  // open: cin, cout
  Comparator #(.width(4), .mode("unsigned")) comparator_1 (
    .a(current_column), .b(4'b1111), .gt(comparator_1_gt));  // open: eq, lt
  Register #(.width(16)) register_2 (.D(column), .en(decoder_1_out0), .Q(column_1), .clk(clk));  // open: clr
  Register #(.width(16)) register_3 (.D(column), .en(decoder_1_out1), .Q(column_2), .clk(clk));  // open: clr
  and and_1 (and_1_out, clk, change_matrix);
  Register #(.width(16)) register_4 (.D(column), .en(decoder_1_out3), .Q(column_4), .clk(clk));  // open: clr
  Register #(.width(16)) register_5 (.D(column), .en(decoder_1_out2), .Q(column_3), .clk(clk));  // open: clr
  Register #(.width(16)) register_6 (.D(column), .en(decoder_1_out4), .Q(column_5), .clk(clk));  // open: clr
  Decoder #(.select(4), .disabled(0)) decoder_1 (
    .out0(decoder_1_out0), .out1(decoder_1_out1), .out2(decoder_1_out2), .out3(decoder_1_out3),
    .out4(decoder_1_out4), .out5(decoder_1_out5), .out6(decoder_1_out6), .out7(decoder_1_out7),
    .out8(decoder_1_out8), .out9(decoder_1_out9), .out10(decoder_1_out10), .out11(decoder_1_out11),
    .out12(decoder_1_out12), .out13(decoder_1_out13), .out14(decoder_1_out14), .out15(decoder_1_out15),
    .sel(current_column), .en(change_matrix));
  Register #(.width(16)) register_7 (.D(column), .en(decoder_1_out5), .Q(column_6), .clk(clk));  // open: clr
  Register #(.width(16)) register_8 (.D(column), .en(decoder_1_out7), .Q(column_8), .clk(clk));  // open: clr
  Register #(.width(16)) register_9 (.D(column), .en(decoder_1_out6), .Q(column_7), .clk(clk));  // open: clr
  Register #(.width(16)) register_10 (.D(column), .en(decoder_1_out8), .Q(column_9), .clk(clk));  // open: clr
  Register #(.width(16)) register_11 (.D(column), .en(decoder_1_out9), .Q(column_10), .clk(clk));  // open: clr
  Register #(.width(16)) register_12 (.D(column), .en(decoder_1_out10), .Q(column_11), .clk(clk));  // open: clr
  Register #(.width(16)) register_13 (.D(column), .en(decoder_1_out11), .Q(column_12), .clk(clk));  // open: clr
  Register #(.width(16)) register_14 (.D(column), .en(decoder_1_out12), .Q(column_13), .clk(clk));  // open: clr
  Register #(.width(16)) register_15 (.D(column), .en(decoder_1_out13), .Q(column_14), .clk(clk));  // open: clr
  Register #(.width(16)) register_16 (.D(column), .en(decoder_1_out15), .Q(column_16), .clk(clk));  // open: clr
  Register #(.width(16)) register_17 (.D(column), .en(decoder_1_out14), .Q(column_15), .clk(clk));  // open: clr
endmodule

module select_matrix (
  input  [5:0] bus_0,
  output out_2,
  output out_3,
  output out_4,
  output out_5,
  output out_6,
  output out_7,
  output out_8,
  output out_9,
  output out_10,
  output out_11,
  output out_12,
  output out_13,
  output out_14,
  output out_15,
  output out_16,
  output out_17,
  output out_18,
  output out_19,
  output out_20,
  output out_21,
  output out_22,
  output out_23,
  output out_24,
  output out_25,
  output out_26,
  output out_27,
  output out_28,
  output out_29,
  output out_30,
  output out_31,
  output out_32,
  output out_33,
  output out_34,
  output out_35,
  output out_36,
  output out_37,
  output out_38,
  output out_39,
  output out_40,
  output out_41,
  output out_42,
  output out_43,
  output out_44,
  output out_45,
  output out_46,
  output out_47,
  output out_48,
  output out_49,
  output out_50,
  output out_51,
  output out_52,
  output out_53,
  output out_54,
  output out_55,
  output out_56,
  output out_57,
  output out_58,
  output out_59,
  output out_60,
  output out_61,
  output out_62,
  output out_63,
  output out_64,
  output out_65
);

  wire decoder_1_out0, decoder_1_out1;

  Decoder #(.enable("false")) decoder_1 (.out0(decoder_1_out0), .out1(decoder_1_out1), .sel(bus_0[5]));
  Decoder #(.select(5), .disabled(0)) decoder_2 (
    .out0(out_18), .out1(out_2), .out2(out_19), .out3(out_3), .out4(out_20), .out5(out_4), .out6(out_21),
    .out7(out_5), .out8(out_22), .out9(out_6), .out10(out_23), .out11(out_7), .out12(out_24), .out13(out_8),
    .out14(out_25), .out15(out_9), .out16(out_26), .out17(out_10), .out18(out_27), .out19(out_11),
    .out20(out_28), .out21(out_12), .out22(out_29), .out23(out_13), .out24(out_30), .out25(out_14),
    .out26(out_31), .out27(out_15), .out28(out_32), .out29(out_16), .out30(out_33), .out31(out_17),
    .sel(bus_0[4:0]), .en(decoder_1_out0));
  Decoder #(.select(5), .disabled(0)) decoder_3 (
    .out0(out_50), .out1(out_34), .out2(out_51), .out3(out_35), .out4(out_52), .out5(out_36), .out6(out_53),
    .out7(out_37), .out8(out_54), .out9(out_38), .out10(out_55), .out11(out_39), .out12(out_56),
    .out13(out_40), .out14(out_57), .out15(out_41), .out16(out_58), .out17(out_42), .out18(out_59),
    .out19(out_43), .out20(out_60), .out21(out_44), .out22(out_61), .out23(out_45), .out24(out_62),
    .out25(out_46), .out26(out_63), .out27(out_47), .out28(out_64), .out29(out_48), .out30(out_65),
    .out31(out_49), .sel(bus_0[4:0]), .en(decoder_1_out1));
endmodule

module frame_test (
  input  _8a0,
  input  _8a1,
  input  _8a2,
  input  _8a3,
  input  _8a4,
  input  _8a5,
  input  _8a6,
  input  _8a7,
  input  _8a8,
  input  _8a9,
  input  _8aa,
  input  _8ab,
  input  _8ac,
  input  _8ad,
  input  _8ae,
  input  _8af
);
endmodule

module system_board (
  input  [15:0] stepIN,
  input  IOsignal,
  input  hold,
  input  clk,
  output nothing,
  output check,
  output checkmate,
  output stalemate,
  output invalid,
  output castling,
  output step_inspected,
  output [21:0] stepOUT
);

  wire and_1_out, comparator_1_eq, IOsel, IRQ, mem, not_1_out, not_2_out, not_3_out, read, sel,
       step_inspected_t, word;
  wire [1:0] status;
  wire [14:0] r4;
  wire [15:0] addr, cdm16_1_p20, cdm16_1_p21, controlled_buffer_4_out, data_bus, fp, IN_q, pc, ps, r0, r1,
       r2, r3, sp;
  wire [15:11] r5, r6;

  // Probe on fp
  // Probe on {r6, stepOUT[21:11]}
  // Probe on {r5, stepOUT[10:0]}
  // Probe on {step_inspected, r4[14:4], castling, r4[2:0]}
  // Probe on r3
  // Probe on r2
  // Probe on r1
  // Probe on r0
  // cdm16 cdm16_1: pin names not known; wires that end beside it: IRQ, hold, r0, r1, clk, r2, r3, {step_inspected, r4[14:4], castling, r4[2:0]}, status, {r5, stepOUT[10:0]}, {r6, stepOUT[21:11]}, fp, pc, sp, ps, mem, read, word, addr, cdm16_1_p20, cdm16_1_p21
  // Probe on status
  // Probe on pc
  // Probe on sp
  // Probe on ps
  not not_1 (not_1_out, read);
  assign data_bus = not_1_out ? cdm16_1_p20 : 16'bz;  // Controlled_Buffer controlled_buffer_1
  assign cdm16_1_p21 = read ? data_bus : 16'bz;  // Controlled_Buffer controlled_buffer_2
  // RAM ram_1: pin names not known; wires that end beside it: addr, word, sel, clk, read, data_bus
  and and_1 (and_1_out, status[0], ~status[1]);  // AND_Gate
  Comparator #(.width(16)) comparator_1 (.a(16'h1234), .b(addr), .eq(comparator_1_eq));  // open: gt, lt
  and and_2 (IOsel, comparator_1_eq, mem);
  Register #(.width(16)) IN (.D(stepIN), .Q(IN_q), .clk(clk));  // open: en, clr
  D_Flip_Flop #(.trigger("falling")) d_ff_1 (
    .clk(IOsignal), .D(and_1_out), .Q(IRQ), .reset(not_2_out));  // open: Qn, preset, en
  not not_2 (not_2_out, and_1_out);
  and and_3 (sel, ~IOsel, mem);  // AND_Gate
  not not_3 (not_3_out, step_inspected_t);
  assign data_bus = not_3_out ? controlled_buffer_4_out : 16'bz;  // Controlled_Buffer controlled_buffer_3
  assign controlled_buffer_4_out = IOsel ? IN_q : 16'bz;  // Controlled_Buffer controlled_buffer_4
  Decoder #(.select(3), .disabled(0)) decoder_1 (
    .out0(nothing), .out1(check), .out2(checkmate), .out3(stalemate), .out4(invalid), .sel(r4[2:0]),
    .en(step_inspected_t));  // open: out5, out6, out7
  // also tied to GND on the sheet: {stepIN[0], stepIN[1], stepIN[2], stepIN[3], stepIN[4], stepIN[5], stepIN[6], stepIN[7], stepIN[8], stepIN[9], stepIN[10], stepIN[11], stepIN[13], stepIN[14], stepIN[15]}
  // also tied to VCC on the sheet: stepIN[12]

  // Other names for the same wires on the sheet: r4 (some bits) = {step_inspected, castling};
  //   r5[10:0] = stepOUT[10:0]; r6[10:0] = stepOUT[21:11]

  // Notes on the sheet:
  //   IOaddr
  //   Interrupt down
endmodule
